# Fritzing sketch MiniGolfer (saved by Fritzing 1.0.1rc)
breadboards: 1

parts:
  Raspberry_Pi_1 = Raspberry Pi 3 [part_number=RPI-3-V1.2]
  Adafruit_OV5640_Camera_Breakout1 = Adafruit OV5640 Camera Breakout [part_number=#5673]  # not connected
  BATT1 = 4xAA Switchable Battery Pack w/Bare Wire
  BATT2 = 4xAA Switchable Battery Pack w/Bare Wire
  HC-SR04_Sensor_1 = HC-SR04 Ultrasonic Distance Sensor
  HC-SR04_Sensor_2 = HC-SR04 Ultrasonic Distance Sensor
  M1 = DC Mini Metal Gear Motor
  Componente1 = SparkFun Motor Driver TB6612FNG (v11) [part_number=ROB-14451]
  M2 = DC Mini Metal Gear Motor
  BATT3 = LiPoly Battery (1300mAh)  # not connected
  L1 = Solenoid
  KY-1 = Keyes Relay [package=THT]

nets:
  N1: Raspberry_Pi_1.GPIO2, HC-SR04_Sensor_1.ECHO
  N2: Raspberry_Pi_1.GPIO3, HC-SR04_Sensor_1.TRIG
  N3: Raspberry_Pi_1.GPIO4, KY-1.signal
  N4: Raspberry_Pi_1.GPIO6, Componente1.AIN2
  N5: Raspberry_Pi_1.GPIO13, Componente1.PWMB
  N6: Raspberry_Pi_1.GPIO26, Componente1.AIN1
  N7: Raspberry_Pi_1.GPIO20, Componente1.BIN1
  N8: Raspberry_Pi_1.GPIO16, Componente1.BIN2
  N9: Raspberry_Pi_1.GPIO12, Componente1.PWMA
  N10: Raspberry_Pi_1.GPIO15, HC-SR04_Sensor_2.ECHO
  N11: Raspberry_Pi_1.GPIO14, HC-SR04_Sensor_2.TRIG
  GND: Raspberry_Pi_1.GND, BATT1.NEG, HC-SR04_Sensor_1.GND, HC-SR04_Sensor_2.GND, Componente1.GND, L1.pin1, KY-1.ground
  VCC: Raspberry_Pi_1.5V, HC-SR04_Sensor_1.VCC, HC-SR04_Sensor_2.VCC, Componente1.VCC, Componente1.STBY, KY-1.power
  N12: BATT1.POS, BATT2.NEG
  N13: BATT2.POS, Componente1.VM, KY-1.NO
  N14: M1.IN1, Componente1.A02
  N15: M1.IN2, Componente1.A01
  N16: Componente1.B01, M2.IN2
  N17: Componente1.B02, M2.IN1
  N18: L1.pin2, KY-1.C

notes:
  Buscar Pololu TB6612FNG Pinout!!!

custom parts:
  Adafruit OV5640 Camera Breakout: Hobby-level microcontrollers are finally getting big and powerful enough to start handling camera modules that historically would have required a full computer or FPGA to handle. The RP2040 and ESP32-Sx series of chips, for example, have enough pins to communicate with the 8-bit data output, DMA to quickly grab a frame, and the necessary RAM to buffer a raw snapshot. Now all we need is a nice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
  4xAA Switchable Battery Pack w/Bare Wire: 4xAA Switchable Battery Pack with Bare Wire connection
  SparkFun Motor Driver TB6612FNG (v11): The TB6612FNG Motor Driver can control up to two DC motors at a constant current of 1.2A (3.2A peak). Two input signals (IN1 and IN2) can be used to control the motor in one of four function modes: CW, CCW, short-brake and stop. The two motor outputs (A and B) can be separately controlled, and the speed of each motor is controlled via a PWM input signal with a frequency up to 100kHz. The STBY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
  LiPoly Battery (1300mAh): Lithium Ion Polymer Battery (1300mAh)
  Keyes Relay: The Keyes 5V relay module is suitable for SCM development, home appliance control. It uses a 5V~12V TIL control signal which can control DC / AC signal.
